// Logisim project cpu.circ as structural Verilog
module full_adder (
  input  IN_A,
  input  IN_B,
  input  IN_Carry,
  output Out_Carry,
  output Sum
);

  wire and_1_out, and_2_out, and_3_out;

  and and_1 (and_1_out, IN_A, IN_B);
  and and_2 (and_2_out, IN_A, IN_Carry);
  and and_3 (and_3_out, IN_B, IN_Carry);
  xor xor_1 (Sum, IN_A, IN_B, IN_Carry);
  or or_1 (Out_Carry, and_1_out, and_2_out, and_3_out);
endmodule

module adder4 (
  input  [3:0] IN_A,
  input  [3:0] IN_B,
  input  IN_Carry,
  output Out_Carry,
  output b3,
  output b2,
  output b1,
  output b0
);

  wire full_adder_2_out_carry, full_adder_3_out_carry, full_adder_4_out_carry;

  full_adder full_adder_1 (
    .IN_A(IN_A[3]), .IN_B(IN_B[3]), .IN_Carry(full_adder_2_out_carry), .Out_Carry(Out_Carry), .Sum(b3));
  full_adder full_adder_2 (
    .IN_A(IN_A[2]), .IN_B(IN_B[2]), .IN_Carry(full_adder_3_out_carry), .Out_Carry(full_adder_2_out_carry),
    .Sum(b2));
  full_adder full_adder_3 (
    .IN_A(IN_A[1]), .IN_B(IN_B[1]), .IN_Carry(full_adder_4_out_carry), .Out_Carry(full_adder_3_out_carry),
    .Sum(b1));
  full_adder full_adder_4 (
    .IN_A(IN_A[0]), .IN_B(IN_B[0]), .IN_Carry(IN_Carry), .Out_Carry(full_adder_4_out_carry), .Sum(b0));
endmodule

module adder16 (
  input  [15:0] IN_A,
  input  [15:0] IN_B,
  input  IN_Carry,
  output Out_Carry,
  output [15:0] Sum
);

  wire adder4_2_out_carry, adder4_3_out_carry, adder4_4_out_carry;

  adder4 adder4_1 (
    .IN_A(IN_A[15:12]), .IN_B(IN_B[15:12]), .IN_Carry(adder4_2_out_carry), .Out_Carry(Out_Carry),
    .b3(Sum[15]), .b2(Sum[14]), .b1(Sum[13]), .b0(Sum[12]));
  adder4 adder4_2 (
    .IN_A(IN_A[11:8]), .IN_B(IN_B[11:8]), .IN_Carry(adder4_3_out_carry), .Out_Carry(adder4_2_out_carry),
    .b3(Sum[11]), .b2(Sum[10]), .b1(Sum[9]), .b0(Sum[8]));
  adder4 adder4_3 (
    .IN_A(IN_A[7:4]), .IN_B(IN_B[7:4]), .IN_Carry(adder4_4_out_carry), .Out_Carry(adder4_3_out_carry),
    .b3(Sum[7]), .b2(Sum[6]), .b1(Sum[5]), .b0(Sum[4]));
  adder4 adder4_4 (
    .IN_A(IN_A[3:0]), .IN_B(IN_B[3:0]), .IN_Carry(IN_Carry), .Out_Carry(adder4_4_out_carry), .b3(Sum[3]),
    .b2(Sum[2]), .b1(Sum[1]), .b0(Sum[0]));
endmodule

module subtractor16 (
  input  [15:0] IN_A,
  input  [15:0] IN_B,
  output [15:0] Sum
);

  wire [15:0] not_1_out;

  assign not_1_out = ~IN_B;  // NOT_Gate not_1, 16 bits wide
  adder16 adder16_1 (.IN_A(IN_A), .IN_B(not_1_out), .IN_Carry(1'b1), .Sum(Sum));  // open: Out_Carry
endmodule

module ALU (
  input  [2:0] Operation,
  input  [15:0] IN_A,
  input  [15:0] IN_B,
  output Out_Carry,
  output [15:0] Result
);

  wire [15:0] adder16_1_sum, and_1_out, left_bit_shifter16_1_result, not_1_out, or_1_out,
       right_bit_shifter16_1_result, subtractor16_1_sum;

  adder16 adder16_1 (.IN_A(IN_A), .IN_B(IN_B), .IN_Carry(1'b0), .Out_Carry(Out_Carry), .Sum(adder16_1_sum));
  subtractor16 subtractor16_1 (.IN_A(IN_A), .IN_B(IN_B), .Sum(subtractor16_1_sum));
  left_bit_shifter16 left_bit_shifter16_1 (.IN_A(IN_A), .Result(left_bit_shifter16_1_result));
  right_bit_shifter16 right_bit_shifter16_1 (.IN_A(IN_A), .Result(right_bit_shifter16_1_result));
  assign and_1_out = IN_A & IN_B;  // AND_Gate and_1, 16 bits wide
  assign or_1_out = IN_A | IN_B;  // OR_Gate or_1, 16 bits wide
  assign not_1_out = ~IN_A;  // NOT_Gate not_1, 16 bits wide
  demultiplexer16_8x1 demultiplexer16_8x1_1 (
    .Addr(Operation), .IN_0(adder16_1_sum), .IN_1(subtractor16_1_sum), .IN_2(left_bit_shifter16_1_result),
    .IN_3(right_bit_shifter16_1_result), .IN_4(and_1_out), .IN_5(or_1_out), .IN_6(not_1_out), .Result(Result));  // open: IN_7
endmodule

module left_bit_shifter16 (
  input  [15:0] IN_A,
  output [15:0] Result
);


  assign Result = {IN_A[14:0], 1'b0};
  // also tied to GND on the sheet: IN_A[15]
endmodule

module right_bit_shifter16 (
  input  [15:0] IN_A,
  output [15:0] Result
);


  assign Result = {1'b0, IN_A[15:1]};
  // also tied to GND on the sheet: IN_A[0]
endmodule

module decoder_3x8 (
  input  [2:0] IN_A,
  output Out_0,
  output Out_1,
  output Out_2,
  output Out_3,
  output Out_4,
  output Out_5,
  output Out_6,
  output Out_7
);

  and and_1 (Out_0, ~IN_A[2], ~IN_A[1], ~IN_A[0]);  // AND_Gate
  and and_2 (Out_1, ~IN_A[2], ~IN_A[1], IN_A[0]);  // AND_Gate
  and and_3 (Out_2, ~IN_A[2], IN_A[1], ~IN_A[0]);  // AND_Gate
  and and_4 (Out_3, ~IN_A[2], IN_A[1], IN_A[0]);  // AND_Gate
  and and_5 (Out_4, IN_A[2], ~IN_A[1], ~IN_A[0]);  // AND_Gate
  and and_6 (Out_5, IN_A[2], ~IN_A[1], IN_A[0]);  // AND_Gate
  and and_7 (Out_6, IN_A[2], IN_A[1], ~IN_A[0]);  // AND_Gate
  and and_8 (Out_7, IN_A[2], IN_A[1], IN_A[0]);
endmodule

module demultiplexer16_8x1 (
  input  [2:0] Addr,
  input  [15:0] IN_0,
  input  [15:0] IN_1,
  input  [15:0] IN_2,
  input  [15:0] IN_3,
  input  [15:0] IN_4,
  input  [15:0] IN_5,
  input  [15:0] IN_6,
  input  [15:0] IN_7,
  output [15:0] Result
);

  wire decoder_3x8_1_out_0, decoder_3x8_1_out_1, decoder_3x8_1_out_2, decoder_3x8_1_out_3,
       decoder_3x8_1_out_4, decoder_3x8_1_out_5, decoder_3x8_1_out_6, decoder_3x8_1_out_7;

  decoder_3x8 decoder_3x8_1 (
    .IN_A(Addr), .Out_0(decoder_3x8_1_out_0), .Out_1(decoder_3x8_1_out_1), .Out_2(decoder_3x8_1_out_2),
    .Out_3(decoder_3x8_1_out_3), .Out_4(decoder_3x8_1_out_4), .Out_5(decoder_3x8_1_out_5),
    .Out_6(decoder_3x8_1_out_6), .Out_7(decoder_3x8_1_out_7));
  assign Result = decoder_3x8_1_out_0 ? IN_0 : 16'bz;  // Controlled_Buffer controlled_buffer_1
  assign Result = decoder_3x8_1_out_1 ? IN_1 : 16'bz;  // Controlled_Buffer controlled_buffer_2
  assign Result = decoder_3x8_1_out_2 ? IN_2 : 16'bz;  // Controlled_Buffer controlled_buffer_3
  assign Result = decoder_3x8_1_out_3 ? IN_3 : 16'bz;  // Controlled_Buffer controlled_buffer_4
  assign Result = decoder_3x8_1_out_4 ? IN_4 : 16'bz;  // Controlled_Buffer controlled_buffer_5
  assign Result = decoder_3x8_1_out_5 ? IN_5 : 16'bz;  // Controlled_Buffer controlled_buffer_6
  assign Result = decoder_3x8_1_out_6 ? IN_6 : 16'bz;  // Controlled_Buffer controlled_buffer_7
  assign Result = decoder_3x8_1_out_7 ? IN_7 : 16'bz;  // Controlled_Buffer controlled_buffer_8
endmodule

module d_flip_flop (
  input  EN,
  input  S,
  output Q
);

  wire and_1_out, and_2_out, nor_2_out, not_1_out;

  not not_1 (not_1_out, S);
  and and_1 (and_1_out, not_1_out, EN);
  and and_2 (and_2_out, EN, S);
  nor nor_1 (Q, and_1_out, nor_2_out);
  nor nor_2 (nor_2_out, Q, and_2_out);
endmodule

module register16 (
  input  [15:0] in_1,
  input  in_2,
  output [15:0] out_3
);

  d_flip_flop d_flip_flop_1 (.EN(in_2), .S(in_1[15]), .Q(out_3[15]));
  d_flip_flop d_flip_flop_2 (.EN(in_2), .S(in_1[14]), .Q(out_3[14]));
  d_flip_flop d_flip_flop_3 (.EN(in_2), .S(in_1[13]), .Q(out_3[13]));
  d_flip_flop d_flip_flop_4 (.EN(in_2), .S(in_1[12]), .Q(out_3[12]));
  d_flip_flop d_flip_flop_5 (.EN(in_2), .S(in_1[11]), .Q(out_3[11]));
  d_flip_flop d_flip_flop_6 (.EN(in_2), .S(in_1[10]), .Q(out_3[10]));
  d_flip_flop d_flip_flop_7 (.EN(in_2), .S(in_1[9]), .Q(out_3[9]));
  d_flip_flop d_flip_flop_8 (.EN(in_2), .S(in_1[8]), .Q(out_3[8]));
  d_flip_flop d_flip_flop_9 (.EN(in_2), .S(in_1[7]), .Q(out_3[7]));
  d_flip_flop d_flip_flop_10 (.EN(in_2), .S(in_1[6]), .Q(out_3[6]));
  d_flip_flop d_flip_flop_11 (.EN(in_2), .S(in_1[5]), .Q(out_3[5]));
  d_flip_flop d_flip_flop_12 (.EN(in_2), .S(in_1[4]), .Q(out_3[4]));
  d_flip_flop d_flip_flop_13 (.EN(in_2), .S(in_1[3]), .Q(out_3[3]));
  d_flip_flop d_flip_flop_14 (.EN(in_2), .S(in_1[2]), .Q(out_3[2]));
  d_flip_flop d_flip_flop_15 (.EN(in_2), .S(in_1[1]), .Q(out_3[1]));
  d_flip_flop d_flip_flop_16 (.EN(in_2), .S(in_1[0]), .Q(out_3[0]));
endmodule
